// Digital circuit RippleCarryAdder.dig as structural Verilog
module RippleCarryAdder (
  input  A0,
  input  A1,
  input  A2,
  input  A3,
  input  B0,
  input  B1,
  input  B2,
  input  B3,
  input  C_in,
  output S0,
  output S1,
  output S2,
  output S3,
  output C_Out
);

  wire Adder0_c_o, Adder1_c_o, Adder2_c_o;

  Add Adder3 (.a(A3), .b(B2), .c_i(Adder2_c_o), .s(S3), .c_o(C_Out));
  Add Adder2 (.a(A2), .b(B2), .c_i(Adder1_c_o), .s(S2), .c_o(Adder2_c_o));
  Add Adder1 (.a(A1), .b(B1), .c_i(Adder0_c_o), .s(S1), .c_o(Adder1_c_o));
  Add Adder0 (.a(A0), .b(B0), .c_i(C_in), .s(S0), .c_o(Adder0_c_o));

  assign B3 = B2;
endmodule

/* Test case:
A3	A2	A1	A0	B3	B2	B1	B0	C_Out	S3	S2	S1	S0
0	0	0	0	0	0	0	0	0	0	0	0	0
0	0	0	1	0	0	0	0	0	0	0	0	1
0	0	1	0	0	0	0	0	0	0	0	1	0
0	0	1	1	0	0	0	0	0	0	0	1	1
0	1	0	0	0	0	0	0	0	0	1	0	0
0	1	0	1	0	0	0	0	0	0	1	0	1
0	1	1	0	0	0	0	0	0	0	1	1	0
0	1	1	1	0	0	0	0	0	0	1	1	1
1	0	0	0	0	0	0	0	0	1	0	0	0
1	0	0	1	0	0	0	0	0	1	0	0	1
1	0	1	0	0	0	0	0	0	1	0	1	0
1	0	1	1	0	0	0	0	0	1	0	1	1
1	1	0	0	0	0	0	0	0	1	1	0	0
1	1	0	1	0	0	0	0	0	1	1	0	1
1	1	1	0	0	0	0	0	0	1	1	1	0
1	1	1	1	0	0	0	0	0	1	1	1	1
0	0	0	0	0	0	0	1	0	0	0	0	1
0	0	0	1	0	0	0	1	0	0	0	1	0
0	0	1	0	0	0	0	1	0	0	0	1	1
0	0	1	1	0	0	0	1	0	0	1	0	0
0	1	0	0	0	0	0	1	0	0	1	0	1
0	1	0	1	0	0	0	1	0	0	1	1	0
0	1	1	0	0	0	0	1	0	0	1	1	1
0	1	1	1	0	0	0	1	0	1	0	0	0
1	0	0	0	0	0	0	1	0	1	0	0	1
1	0	0	1	0	0	0	1	0	1	0	1	0
1	0	1	0	0	0	0	1	0	1	0	1	1
1	0	1	1	0	0	0	1	0	1	1	0	0
1	1	0	0	0	0	0	1	0	1	1	0	1
1	1	0	1	0	0	0	1	0	1	1	1	0
1	1	1	0	0	0	0	1	0	1	1	1	1
1	1	1	1	0	0	0	1	1	0	0	0	0
0	0	0	0	0	0	1	0	0	0	0	1	0
0	0	0	1	0	0	1	0	0	0	0	1	1
0	0	1	0	0	0	1	0	0	0	1	0	0
0	0	1	1	0	0	1	0	0	0	1	0	1
0	1	0	0	0	0	1	0	0	0	1	1	0
0	1	0	1	0	0	1	0	0	0	1	1	1
0	1	1	0	0	0	1	0	0	1	0	0	0
0	1	1	1	0	0	1	0	0	1	0	0	1
1	0	0	0	0	0	1	0	0	1	0	1	0
1	0	0	1	0	0	1	0	0	1	0	1	1
1	0	1	0	0	0	1	0	0	1	1	0	0
1	0	1	1	0	0	1	0	0	1	1	0	1
1	1	0	0	0	0	1	0	0	1	1	1	0
1	1	0	1	0	0	1	0	0	1	1	1	1
1	1	1	0	0	0	1	0	1	0	0	0	0
1	1	1	1	0	0	1	0	1	0	0	0	1
0	0	0	0	0	0	1	1	0	0	0	1	1
0	0	0	1	0	0	1	1	0	0	1	0	0
0	0	1	0	0	0	1	1	0	0	1	0	1
0	0	1	1	0	0	1	1	0	0	1	1	0
0	1	0	0	0	0	1	1	0	0	1	1	1
0	1	0	1	0	0	1	1	0	1	0	0	0
0	1	1	0	0	0	1	1	0	1	0	0	1
0	1	1	1	0	0	1	1	0	1	0	1	0
1	0	0	0	0	0	1	1	0	1	0	1	1
1	0	0	1	0	0	1	1	0	1	1	0	0
1	0	1	0	0	0	1	1	0	1	1	0	1
1	0	1	1	0	0	1	1	0	1	1	1	0
1	1	0	0	0	0	1	1	0	1	1	1	1
1	1	0	1	0	0	1	1	1	0	0	0	0
1	1	1	0	0	0	1	1	1	0	0	0	1
1	1	1	1	0	0	1	1	1	0	0	1	0
0	0	0	0	0	1	0	0	0	0	1	0	0
0	0	0	1	0	1	0	0	0	0	1	0	1
0	0	1	0	0	1	0	0	0	0	1	1	0
0	0	1	1	0	1	0	0	0	0	1	1	1
0	1	0	0	0	1	0	0	0	1	0	0	0
0	1	0	1	0	1	0	0	0	1	0	0	1
0	1	1	0	0	1	0	0	0	1	0	1	0
0	1	1	1	0	1	0	0	0	1	0	1	1
1	0	0	0	0	1	0	0	0	1	1	0	0
1	0	0	1	0	1	0	0	0	1	1	0	1
1	0	1	0	0	1	0	0	0	1	1	1	0
1	0	1	1	0	1	0	0	0	1	1	1	1
1	1	0	0	0	1	0	0	1	0	0	0	0
1	1	0	1	0	1	0	0	1	0	0	0	1
1	1	1	0	0	1	0	0	1	0	0	1	0
1	1	1	1	0	1	0	0	1	0	0	1	1
0	0	0	0	0	1	0	1	0	0	1	0	1
0	0	0	1	0	1	0	1	0	0	1	1	0
0	0	1	0	0	1	0	1	0	0	1	1	1
0	0	1	1	0	1	0	1	0	1	0	0	0
0	1	0	0	0	1	0	1	0	1	0	0	1
0	1	0	1	0	1	0	1	0	1	0	1	0
0	1	1	0	0	1	0	1	0	1	0	1	1
0	1	1	1	0	1	0	1	0	1	1	0	0
1	0	0	0	0	1	0	1	0	1	1	0	1
1	0	0	1	0	1	0	1	0	1	1	1	0
1	0	1	0	0	1	0	1	0	1	1	1	1
1	0	1	1	0	1	0	1	1	0	0	0	0
1	1	0	0	0	1	0	1	1	0	0	0	1
1	1	0	1	0	1	0	1	1	0	0	1	0
1	1	1	0	0	1	0	1	1	0	0	1	1
1	1	1	1	0	1	0	1	1	0	1	0	0
0	0	0	0	0	1	1	0	0	0	1	1	0
0	0	0	1	0	1	1	0	0	0	1	1	1
0	0	1	0	0	1	1	0	0	1	0	0	0
0	0	1	1	0	1	1	0	0	1	0	0	1
0	1	0	0	0	1	1	0	0	1	0	1	0
0	1	0	1	0	1	1	0	0	1	0	1	1
0	1	1	0	0	1	1	0	0	1	1	0	0
0	1	1	1	0	1	1	0	0	1	1	0	1
1	0	0	0	0	1	1	0	0	1	1	1	0
1	0	0	1	0	1	1	0	0	1	1	1	1
1	0	1	0	0	1	1	0	1	0	0	0	0
1	0	1	1	0	1	1	0	1	0	0	0	1
1	1	0	0	0	1	1	0	1	0	0	1	0
1	1	0	1	0	1	1	0	1	0	0	1	1
1	1	1	0	0	1	1	0	1	0	1	0	0
1	1	1	1	0	1	1	0	1	0	1	0	1
0	0	0	0	0	1	1	1	0	0	1	1	1
0	0	0	1	0	1	1	1	0	1	0	0	0
0	0	1	0	0	1	1	1	0	1	0	0	1
0	0	1	1	0	1	1	1	0	1	0	1	0
0	1	0	0	0	1	1	1	0	1	0	1	1
0	1	0	1	0	1	1	1	0	1	1	0	0
0	1	1	0	0	1	1	1	0	1	1	0	1
0	1	1	1	0	1	1	1	0	1	1	1	0
1	0	0	0	0	1	1	1	0	1	1	1	1
1	0	0	1	0	1	1	1	1	0	0	0	0
1	0	1	0	0	1	1	1	1	0	0	0	1
1	0	1	1	0	1	1	1	1	0	0	1	0
1	1	0	0	0	1	1	1	1	0	0	1	1
1	1	0	1	0	1	1	1	1	0	1	0	0
1	1	1	0	0	1	1	1	1	0	1	0	1
1	1	1	1	0	1	1	1	1	0	1	1	0
0	0	0	0	1	0	0	0	0	1	0	0	0
0	0	0	1	1	0	0	0	0	1	0	0	1
0	0	1	0	1	0	0	0	0	1	0	1	0
0	0	1	1	1	0	0	0	0	1	0	1	1
0	1	0	0	1	0	0	0	0	1	1	0	0
0	1	0	1	1	0	0	0	0	1	1	0	1
0	1	1	0	1	0	0	0	0	1	1	1	0
0	1	1	1	1	0	0	0	0	1	1	1	1
1	0	0	0	1	0	0	0	1	0	0	0	0
1	0	0	1	1	0	0	0	1	0	0	0	1
1	0	1	0	1	0	0	0	1	0	0	1	0
1	0	1	1	1	0	0	0	1	0	0	1	1
1	1	0	0	1	0	0	0	1	0	1	0	0
1	1	0	1	1	0	0	0	1	0	1	0	1
1	1	1	0	1	0	0	0	1	0	1	1	0
1	1	1	1	1	0	0	0	1	0	1	1	1
0	0	0	0	1	0	0	1	0	1	0	0	1
0	0	0	1	1	0	0	1	0	1	0	1	0
0	0	1	0	1	0	0	1	0	1	0	1	1
0	0	1	1	1	0	0	1	0	1	1	0	0
0	1	0	0	1	0	0	1	0	1	1	0	1
0	1	0	1	1	0	0	1	0	1	1	1	0
0	1	1	0	1	0	0	1	0	1	1	1	1
0	1	1	1	1	0	0	1	1	0	0	0	0
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*/
